# Fritzing sketch RFID-RC522 (saved by Fritzing 0.9.3b)
breadboards: 1

parts:
  Part2 = RFID-RC522-v2
  Part1 = Arduino Uno (Rev3) - ICSP
  LED1 = LED - 5mm [color="Red (633nm)" package="5 mm [THT]"]
  LED2 = smd LED [color="Green (555nm)" package="0805 [SMD]"]
  R1 = Resistor [tolerance=±5% resistance=220 package=THT]
  R2 = Resistor [tolerance=±5% resistance=220 package=THT]

nets:
  N1: Part2.SDA, Part1.D10_PWM/SS
  N2: Part2.SCK, Part1.D13/SCK
  N3: Part2.MOSI, Part1.D11_PWM/MOSI
  N4: Part2.MISO, Part1.D12/MISO
  GND: Part2.GND, Part1.GND, LED1.cathode, LED2.cathode
  N5: Part2.RST, Part1.D9_PWM
  N6: Part2.3_3V, Part1.3V3
  N7: Part1.D2, R1.Pin_1
  N8: Part1.D3_PWM, R2.Pin_1
  N9: LED1.anode, R2.Pin_0
  N10: LED2.anode, R1.Pin_0

custom parts:
  RFID-RC522-v2: A simple China made RFID-RC522 Reader; do check the pin labels, as this is a MFRC522 based clone.
